// Digital circuit lc3.dig as structural Verilog
module lc3 (
  input  Clk
);

  wire ACV, ADDR1MUX, and_1_out, and_2_out, and_3_out, BEN, GateALU, GateMARMUX, GateMDR, GatePC, GateSP,
       lc3_cc_logic_1_n, lc3_cc_logic_1_p, lc3_cc_logic_1_z, LD_BEN, LD_CC, LD_DDR, LD_DSR, LD_IR, LD_KBSR,
       LD_MAR, LD_MDR, LD_PC, LD_Priv, LD_REG, LD_SavedSSP, LD_SavedUSP, MARMUX, MEM_EN, MIO_EN, N, or_1_out,
       P, Priv, PSR_15, PSRMux, R, R_W, Set_Priv, SR2MUX, Z;
  wire [1:0] ADDR2MUX, ALUK, MDR_Select, PCMUX, SPMUX, SR1MUX;
  wire [2:0] DR_nzp, driver_1_out_2, multiplexer_9_out, SR1;
  wire [3:0] driver_1_out_3;
  wire [4:0] Immed;
  wire [4:1] IR_15_11;
  wire [5:0] lc3_control_1_state;
  wire [8:0] driver_1_out;
  wire [15:0] D_in, D_out, DSR, INMUX_out, KBDR, KBSR, keyboard_1_d, lc3_alu_1_alu, lc3_alu_2_alu,
       lc3_memory_1_p7, lc3_register_file_1_sr2_out, multiplexer_1_out, multiplexer_2_out, multiplexer_3_out,
       multiplexer_5_out, multiplexer_7_out, multiplexer_8_out, multiplexer_10_out, PC, plus_1_s,
       Saved_SSP_q, Saved_USP_q, SEXT_2_out, SEXT_3_out, SEXT_4_out, SEXT_out, SR1_OUT;
  wire [15:15] KB_Data;

  Register u_BEN (.D(or_1_out), .C(Clk), .en(LD_BEN), .Q(BEN));
  or or_1 (or_1_out, and_3_out, and_2_out, and_1_out);
  // Probe on {IR_15_11, DR_nzp, SR1, SR2MUX, Immed}
  and and_1 (and_1_out, DR_nzp[2], N);
  and and_2 (and_2_out, DR_nzp[1], Z);
  and and_3 (and_3_out, DR_nzp[0], P);
  Register #(.Bits(16)) IR (
    .D({driver_1_out_3, driver_1_out_2, driver_1_out}), .C(Clk), .en(LD_IR),
    .Q({IR_15_11, DR_nzp, SR1, SR2MUX, Immed}));
  BitExtender #(.inputBits(6)) SEXT (.in({SR2MUX, Immed}), .out(SEXT_out));
  BitExtender #(.inputBits(9)) SEXT_2 (.in({SR1, SR2MUX, Immed}), .out(SEXT_2_out));
  BitExtender #(.inputBits(11)) SEXT_3 (.in({DR_nzp[1:0], SR1, SR2MUX, Immed}), .out(SEXT_3_out));
  lc3_acv lc3_acv_1 (.mode(PSR_15), .opcode(driver_1_out_3), .nzp(driver_1_out_2), .ACV(ACV));
  assign {driver_1_out_3, driver_1_out_2, driver_1_out} = GateMARMUX ? multiplexer_1_out : 16'bz;  // Driver driver_1
  Multiplexer #(.Bits(16)) multiplexer_1 (
    .sel(MARMUX), .in_0({{8{1'b0}}, SR1[1:0], SR2MUX, Immed}), .in_1(lc3_alu_1_alu), .out(multiplexer_1_out));
  Register u_Priv (.D(Priv), .C(Clk), .en(LD_Priv), .Q(PSR_15));
  Multiplexer #(.Selector_Bits(2), .Bits(16)) multiplexer_2 (
    .sel(ADDR2MUX), .in_0({16{1'b0}}), .in_1(SEXT_out), .in_2(SEXT_2_out), .in_3(SEXT_3_out),
    .out(multiplexer_2_out));
  Multiplexer #(.Bits(16)) multiplexer_3 (.sel(ADDR1MUX), .in_0(PC), .in_1(SR1_OUT), .out(multiplexer_3_out));
  LED u_N (.in(N));
  Register N_2 (.D(lc3_cc_logic_1_n), .C(Clk), .en(LD_CC), .Q(N));
  Multiplexer multiplexer_4 (.sel(PSRMux), .in_0(Set_Priv), .in_1(driver_1_out_3[3]), .out(Priv));
  lc3_alu lc3_alu_1 (.ALU(lc3_alu_1_alu), .A(multiplexer_2_out), .B(multiplexer_3_out), .ALUK(2'b00));
  Register u_Z (.D(lc3_cc_logic_1_z), .C(Clk), .en(LD_CC), .Q(Z));
  lc3_cc_logic lc3_cc_logic_1 (
    .D_in({driver_1_out_3, driver_1_out_2, driver_1_out}), .N(lc3_cc_logic_1_n), .Z(lc3_cc_logic_1_z),
    .P(lc3_cc_logic_1_p));
  assign {driver_1_out_3, driver_1_out_2, driver_1_out} = GateMDR ? D_in : 16'bz;  // Driver driver_2
  LED Z_2 (.in(Z));
  Multiplexer #(.Bits(16)) multiplexer_5 (
    .sel(MIO_EN), .in_0({driver_1_out_3, driver_1_out_2, driver_1_out}), .in_1(INMUX_out),
    .out(multiplexer_5_out));
  Register #(.Bits(16)) MDR (.D(multiplexer_5_out), .C(Clk), .en(LD_MDR), .Q(D_in));
  // Probe on D_in
  LED u_P (.in(P));
  Register P_2 (.D(lc3_cc_logic_1_p), .C(Clk), .en(LD_CC), .Q(P));
  lc3_control lc3_control_1 (
    .Clk(Clk), .INT(1'b0), .R(R), .IR_15_11({IR_15_11, DR_nzp[2]}), .BEN(BEN), .PSR_15(PSR_15), .ACV(ACV),
    .LD_MAR(LD_MAR), .LD_MDR(LD_MDR), .LD_IR(LD_IR), .LD_BEN(LD_BEN), .LD_REG(LD_REG), .LD_CC(LD_CC),
    .LD_PC(LD_PC), .LD_Priv(LD_Priv), .LD_SavedSSP(LD_SavedSSP), .LD_SavedUSP(LD_SavedUSP), .GatePC(GatePC),
    .GateMDR(GateMDR), .GateALU(GateALU), .GateMARMUX(GateMARMUX), .GateSP(GateSP), .PCMUX(PCMUX),
    .SR1MUX(SR1MUX), .ADDR2MUX(ADDR2MUX), .SPMUX(SPMUX), .ALUK(ALUK), .ADDR1MUX(ADDR1MUX), .MARMUX(MARMUX),
    .PSRMUX(PSRMux), .MIO_EN(MIO_EN), .R_W(R_W), .Set_Priv(Set_Priv), .State(lc3_control_1_state));  // open: LD_Vector, LD_Priority, LD_ACV, GateVector, GatePC_1, GatePSR, DRMUX, VectorMUX, TableMUX
  // lc3_memory lc3_memory_1: pin names not known; wires that end beside it: R, D_out, Clk, R_W, MEM_EN, D_in, lc3_memory_1_p7
  Multiplexer #(.Selector_Bits(2), .Bits(16)) multiplexer_6 (
    .sel(MDR_Select), .in_0(KBDR), .in_1(KBSR), .in_2(KBDR), .in_3(D_out), .out(INMUX_out));
  lc3_memmap lc3_memmap_1 (
    .addr(lc3_memory_1_p7), .en(MIO_EN), .R_W(R_W), .MDR_Select(MDR_Select), .MEM_EN(MEM_EN),
    .LD_KBSR(LD_KBSR), .LD_DSR(LD_DSR), .LD_DDR(LD_DDR));  // open: R_mapped
  Register #(.Bits(16)) MAR (
    .D({driver_1_out_3, driver_1_out_2, driver_1_out}), .C(Clk), .en(LD_MAR), .Q(lc3_memory_1_p7));
  // Probe on lc3_memory_1_p7
  Add #(.Bits(16)) plus_1 (.a(PC), .b(16'h1), .c_i(1'b0), .s(plus_1_s));  // open: c_o
  // Probe on PC
  Multiplexer #(.Selector_Bits(2), .Bits(16)) multiplexer_7 (
    .sel(PCMUX), .in_0(plus_1_s), .in_1({driver_1_out_3, driver_1_out_2, driver_1_out}),
    .in_2(lc3_alu_1_alu), .in_3({16{1'b0}}), .out(multiplexer_7_out));
  // Probe Bus on {driver_1_out_3, driver_1_out_2, driver_1_out}
  Keyboard keyboard_1 (.C(Clk), .en(1'b1), .D(keyboard_1_d), .av(KB_Data[15]));
  assign {driver_1_out_3, driver_1_out_2, driver_1_out} = GatePC ? PC : 16'bz;  // Driver driver_3
  pc #(.applicationType("IVERILOG"), .CodeFile("/home/allan/cs061/LC3_realized/lc3-pc.v")) u_pc (
    .addr_in(multiplexer_7_out), .clk(Clk), .en(LD_PC), .addr_out(PC));
  Register #(.Bits(16)) u_KBSR (.D({KB_Data[15], {15{1'b0}}}), .C(Clk), .en(LD_KBSR), .Q(KBSR));
  Register #(.Bits(16)) u_KBDR (.D(keyboard_1_d), .C(Clk), .en(KB_Data[15]), .Q(KBDR));
  BitExtender #(.inputBits(5)) SEXT_4 (.in(Immed), .out(SEXT_4_out));
  // Probe State on lc3_control_1_state
  lc3_register_file lc3_register_file_1 (
    .Clk(Clk), .Data({driver_1_out_3, driver_1_out_2, driver_1_out}), .LD_Reg(LD_REG), .DR(DR_nzp),
    .SR1(multiplexer_9_out), .SR2(Immed[2:0]), .SR2_OUT(lc3_register_file_1_sr2_out), .SR1_OUT(SR1_OUT));
  Multiplexer #(.Bits(16)) multiplexer_8 (
    .sel(SR2MUX), .in_0(lc3_register_file_1_sr2_out), .in_1(SEXT_4_out), .out(multiplexer_8_out));
  lc3_alu lc3_alu_2 (.ALU(lc3_alu_2_alu), .A(SR1_OUT), .B(multiplexer_8_out), .ALUK(ALUK));
  assign {driver_1_out_3, driver_1_out_2, driver_1_out} = GateALU ? lc3_alu_2_alu : 16'bz;  // Driver driver_4
  Multiplexer #(.Selector_Bits(2), .Bits(3)) multiplexer_9 (
    .sel(SR1MUX), .in_0(DR_nzp), .in_1(SR1), .in_2(3'b110), .in_3(3'b000), .out(multiplexer_9_out));
  Register #(.Bits(16)) u_DSR (.D(D_in), .C(Clk), .en(LD_DSR), .Q(DSR));
  Register #(.Bits(16)) DDR (.D(D_in), .C(Clk), .en(LD_DDR));  // open: Q
  Register #(.Bits(16)) Saved_USP (.D(SR1_OUT), .C(Clk), .en(LD_SavedUSP), .Q(Saved_USP_q));
  Register #(.Bits(16)) Saved_SSP (.D(SR1_OUT), .C(Clk), .en(LD_SavedSSP), .Q(Saved_SSP_q));
  Terminal terminal_1 (.D(keyboard_1_d), .C(Clk), .en(1'b1));
  Multiplexer #(.Selector_Bits(2), .Bits(16)) multiplexer_10 (
    .sel(SPMUX), .in_0(Saved_USP_q), .in_1(16'h1), .in_2({16{1'b1}}), .in_3(Saved_SSP_q),
    .out(multiplexer_10_out));
  assign {driver_1_out_3, driver_1_out_2, driver_1_out} = GateSP ? multiplexer_10_out : 16'bz;  // Driver driver_5

  // Other names for the same wires on the sheet: SR2[2:0] = Immed[2:0]; IR_15_11[0] = DR_nzp[2]

  // Notes on the sheet:
  //   Input
  //   Output
endmodule
